# Fritzing sketch 30.007 SYSTEMS DIAG (saved by Fritzing 0.9.3b)

parts:
  U1 = Mini-360 DC-DC Buck converter [package=THT]
  JACK1 = 2.1mm Barrel Jack with Terminal Block
  U2 = prefix0000
  Raspberry_Pi_1 = Raspberry Pi 3 [part_number=RPI-3-V1.2]
  Mod1 = KY-019 5V Relay Module [package="Breakout board"]
  U4 = Mini-360 DC-DC Buck converter [package=THT]
  M1 = Stepper Motor - Bipolar
  M3 = DC Motor
  DS1 = DS18B20 1-Wire Temperature Sensor Probe Cable
  U5 = TCM8240MD [package=tcm8240md]  # not connected
  J1 = Peltier Element
  Mod2 = KY-019 5V Relay Module [package="Breakout board"]
  J3 = Wago 350 4 terminals [part_number="wago 350-4" package=THT]
  J5 = Wago 350 5 terminals [part_number="wago 350-5" package=THT]
  U7 = prefix0000
  M4 = Stepper Motor - Bipolar
  M6 = Stepper Motor - Bipolar
  U10 = prefix0000
  M7 = Stepper Motor - Bipolar
  U11 = prefix0000
  R1 = Resistor [tolerance=±5% resistance=4.7k package=THT]
  D2F1 = D2F-FL Omron Snap Action Limit Switch with Level
  D2F2 = D2F-FL Omron Snap Action Limit Switch with Level
  D2F3 = D2F-FL Omron Snap Action Limit Switch with Level
  J6 = Wago 350 5 terminals [part_number="wago 350-5" package=THT]

nets:
  N1: U1.IN-, Mod1.-, Mod2.-, Mod2.NO, J3.pin2, U10.connector5
  N2: U1.IN+, J5.pin3
  N3: U1.OUT+, M3.pin_2
  N4: U1.OUT-, Mod1.NO
  N5: JACK1.POS, J5.pin1, U10.connector4, U11.connector4
  N6: JACK1.NEG, J3.pin4
  N7: U2.connector0, M1.D
  N8: U2.connector1, M1.C
  N9: U2.connector2, M1.B
  N10: U2.connector3, M1.A
  N11: U2.connector4, J5.pin2, U7.connector4
  N12: U2.connector5, J3.pin1, U7.connector5
  N13: U2.connector6, U2.connector8, U2.connector10, Raspberry_Pi_1.GND, U7.connector6, U7.connector8, U7.connector10, U10.connector6, U10.connector8, U10.connector10, U11.connector6, U11.connector8, U11.connector10
  N14: U2.connector7, Raspberry_Pi_1.GPIO16, U7.connector7, U10.connector7, U11.connector7
  N15: U2.connector9, Raspberry_Pi_1.GPIO20
  N16: U2.connector11, Raspberry_Pi_1.GPIO21
  N17: Raspberry_Pi_1.3v3, J6.pin4
  N18: Raspberry_Pi_1.GPIO2, DS1.DQ, R1.Pin_1
  N19: Raspberry_Pi_1.GPIO4, Mod2.S
  N20: Raspberry_Pi_1.GPIO27, D2F1.NO
  N21: Raspberry_Pi_1.GPIO22, U11.connector11
  N22: Raspberry_Pi_1.GPIO10, U11.connector9
  N23: Raspberry_Pi_1.GPIO9, D2F2.NO
  N24: Raspberry_Pi_1.GPIO11, U10.connector11
  N25: Raspberry_Pi_1.GPIO5, D2F3.NO
  N26: Raspberry_Pi_1.GPIO6, U10.connector9
  N27: Raspberry_Pi_1.GPIO19, U7.connector11
  N28: Raspberry_Pi_1.GPIO26, U7.connector9
  N29: Raspberry_Pi_1.GPIO14, Mod1.S
  N30: Raspberry_Pi_1.5V, Mod1.+, Mod2.+
  N31: Mod1.Common, M3.pin_1
  N32: U4.IN-, J3.pin3
  N33: U4.IN+, J5.pin4
  N34: DS1.VDD, R1.Pin_0, J6.pin5
  N35: J1.pin1, Mod2.Common
  N36: J1.pin2, J5.pin5
  N37: U7.connector0, M4.D
  N38: U7.connector1, M4.C
  N39: U7.connector2, M4.B
  N40: U7.connector3, M4.A
  N41: M6.A, U10.connector3
  N42: M6.C, U10.connector1
  N43: M6.B, U10.connector2
  N44: M6.D, U10.connector0
  N45: M7.A, U11.connector3
  N46: M7.C, U11.connector1
  N47: M7.B, U11.connector2
  N48: M7.D, U11.connector0
  N49: D2F1.COM, J6.pin1
  N50: D2F2.COM, J6.pin2
  N51: D2F3.COM, J6.pin3

notes:
  stepdown 12v to 7v
  input mains
  stepdown 12v to 5v
  (should use this for all 5v applications like relays but can test with 5v from rpi first)
  Pipette
  Centrifuge
  TEC 12v
  stepper x axis
  stepper z axis
  stepper y axis

custom parts:
  Mini-360 DC-DC Buck converter: Mini-360 DC-DC Buck converter. Tiny buck step down voltage converter, input voltage 4.75 to 23V output 1 to 17V adjustable. Available from ebay and the like.
  KY-019 5V Relay Module: KY-019 5V Relay module, used to control AC circuits. (Special thanks to vanepp for fixing the PCB holes and other errors)
  Wago 350 4 terminals: Terminal strip with operating push buttons, RM 3.5 mm, 4-pin
  Wago 350 5 terminals: Terminal strip with operating push buttons, RM 3.5 mm, 5-pin
  D2F-FL Omron Snap Action Limit Switch with Level: Snap action switch with stainless steel lever.
